# Fritzing sketch haswitchv2 (saved by Fritzing 0.9.3b)
circuit board: 6cm x 4cm
breadboards: 1

parts:
  AC-INPUT_JP1 = Header 2 [package=screwterminal-3.5mm-2_lock]
  AC-DC_HLK-PM1 = HLK-PM01
  WeMos_D1_Mini1 = WeMos D1 Mini
  DATA-R1 = RPACK* [package=rpack-sip-pth-5]

nets:
  N1: AC-INPUT_JP1.1, AC-DC_HLK-PM1.AC#0
  N2: AC-INPUT_JP1.2, AC-DC_HLK-PM1.AC#1
  N3: AC-DC_HLK-PM1.-Vo, WeMos_D1_Mini1.G, DATA-R1.5
  N4: AC-DC_HLK-PM1.+Vo, WeMos_D1_Mini1.5V, DATA-R1.6
  N5: WeMos_D1_Mini1.D1, DATA-R1.1
  N6: WeMos_D1_Mini1.D4, DATA-R1.3
  N7: WeMos_D1_Mini1.D7, DATA-R1.4

notes:
  5v
  GRND
  D7
  D4
  D1
